# Fritzing sketch Bedwarmer (saved by Fritzing 1.0.0d)
circuit board: 8.46667cm x 5.64444cm

parts:
  Temp_+ = Momentary Switch [package=ksa_sealed_tac_switch]
  Timer_+ = Momentary Switch [package=ksa_sealed_tac_switch]
  Timer_- = Momentary Switch [package=ksa_sealed_tac_switch]
  Temp_- = Momentary Switch [package=ksa_sealed_tac_switch]
  Solid_State_Relay = RELAY-SOLIDSTATE [package=relay-s108t02]
  M1 = DOIT Esp32 DevKit v1 (30 pins long, 11 pins width) [part_number=ESP32S-PIN30]
  Pulldown_Reistor = Resistor [tolerance=±5% power=0.25W resistance=10k package=THT]
  Load_(Heated_Sheets) = Inductor [current=1A inductance=0H package="400 mil [THT]"]
  Power = Momentary Switch [package=ksa_sealed_tac_switch]
  OLED_I2C2 = OLED 128x64 I2C Monochrome Display
  100-240V_AC_to_5V/700mA_DC = generic-ac-power-supply [package=THT]

nets:
  N1: Temp_+.1, M1.D13
  N2: Temp_+.4, Timer_+.4, Power.3
  N3: Timer_+.1, M1.D14
  N4: Timer_-.1, M1.D27
  N5: Timer_-.3, Temp_-.3, Power.4
  N6: Temp_-.1, M1.D12
  N7: Temp_-.4, Pulldown_Reistor.Pin_1
  N8: Solid_State_Relay.T1, Load_(Heated_Sheets).pin_1
  N9: Solid_State_Relay.T2, 100-240V_AC_to_5V/700mA_DC.pin1
  N10: Solid_State_Relay.+, M1.D23
  GND: Solid_State_Relay.-, M1.GND, Pulldown_Reistor.Pin_0, OLED_I2C2.GND, 100-240V_AC_to_5V/700mA_DC.pin3#2
  3V3: M1.3V3, OLED_I2C2.VDD
  N11: M1.D21, OLED_I2C2.SDA
  N12: M1.D22, OLED_I2C2.SCK
  N13: M1.D26, Power.1
  N14: M1.VIN, 100-240V_AC_to_5V/700mA_DC.pin3#3
  N15: Load_(Heated_Sheets).pin_0, 100-240V_AC_to_5V/700mA_DC.pin2

custom parts:
  DOIT Esp32 DevKit v1 (30 pins long, 11 pins width): The DOIT Esp32 DevKit v1 is one of the development board created by DOIT to evaluate the ESP-WROOM-32 module. It is based on the ESP32 microcontroller that boasts Wifi, Bluetooth, Ethernet and Low Power support all in a single chip. (vanepp) made breadboard work, adjusted pin numbering and labels and reduced size of schematic and cleaned up pcb. This chip is 30pins long (2 x15) and 11 pins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
  generic-ac-power-supply: Generic ac power supply module. Use as is, or customize the svgs to fit your particular device (as they are all different.) Provides AC input and single DC output. PCB is generic and will need modifications if you intend to do a pcb mount.
